# Fritzing sketch wiring (saved by Fritzing 0.9.4)
breadboards: 1

parts:
  Part1 = Arduino Uno (Rev3)
  HC-SR04_Sensor_1 = HC-SR04 Ultrasonic Distance Sensor
  U1 = 74HC595 [package="DIP16 [THT]"]
  LED1 = RGB LED (com. cathode, rbg) [package="5 mm [THT]"]
  LED2 = RGB LED (com. cathode, rbg) [package="5 mm [THT]"]
  R1 = Resistor [tolerance=±5% resistance=220 package="1206 [SMD]"]
  R2 = Resistor [tolerance=±5% resistance=220 package="1206 [SMD]"]
  R3 = Resistor [tolerance=±5% resistance=220 package="1206 [SMD]"]
  R4 = Resistor [tolerance=±5% resistance=220 package="1206 [SMD]"]
  R5 = Resistor [tolerance=±5% resistance=220 package="1206 [SMD]"]
  R6 = Resistor [tolerance=±5% resistance=220 package="1206 [SMD]"]
  Grove1 = Grove OLED 128x96

nets:
  N1: Part1.A4/SDA, Grove1.SDA
  N2: Part1.A5/SCL, Grove1.SCL
  N3: Part1.D9_PWM, U1.SH_CP
  N4: Part1.D10_PWM/SS, U1.OE
  N5: Part1.D11_PWM/MOSI, U1.ST_CP
  N6: Part1.D12/MISO, U1.DS
  N7: Part1.D3_PWM, HC-SR04_Sensor_1.TRIG
  N8: Part1.D4, HC-SR04_Sensor_1.ECHO
  VCC: Part1.5V, HC-SR04_Sensor_1.VCC, U1.MR, U1.VCC, Grove1.VCC
  GND: Part1.GND, HC-SR04_Sensor_1.GND, U1.GND, LED1.common_cathode, LED2.common_cathode, Grove1.GND
  N9: U1.Q1, R1.Pin_0
  N10: U1.Q2, R2.Pin_0
  N11: U1.Q3, R3.Pin_0
  N12: U1.Q4, R4.Pin_0
  N13: U1.Q5, R5.Pin_0
  N14: U1.Q6, R6.Pin_0
  N15: LED1.red_anode, R1.Pin_1
  N16: LED1.blue_anode, R2.Pin_1
  N17: LED1.green_anode, R3.Pin_1
  N18: LED2.red_anode, R4.Pin_1
  N19: LED2.blue_anode, R5.Pin_1
  N20: LED2.green_anode, R6.Pin_1
